# Fritzing sketch Movement_Sketch (saved by Fritzing 0.9.3b)
breadboards: 1

parts:
  IC1 = L293D [package=THT]
  Bauteil1 = Arduino Nano (Rev3.0)
  M1 = DC Motor
  M2 = DC Motor
  VCC1 = Battery block 9V
  IC2 = L293D [package=THT]
  M3 = DC Motor
  Bauteil2 = 24 NeoPixel Ring [part_number=1586]

nets:
  N1: IC1.Enable_1, Bauteil1.D3
  N2: IC1.In_1, Bauteil1.D4
  N3: IC1.Out_1_(_Controlled_by_Enable_1_), M2.pin_2
  N4: IC1.0V, VCC1.-, IC2.0V
  N5: IC1.Out_2_(_Controlled_by_Enable_1_), M2.pin_1
  N6: IC1.In_2, Bauteil1.D5
  N7: IC1.+Vmotor, IC1.+V, VCC1.+, IC2.+V
  N8: IC1.Enable_2, Bauteil1.D6
  N9: IC1.In_3, Bauteil1.D7
  N10: IC1.Out_3_(_Controlled_by_Enable_2_), M1.pin_1
  N11: IC1.Out_4_(_Controlled_by_Enable_2_), M1.pin_2
  N12: IC1.In_4, Bauteil1.D8
  GND: Bauteil1.GND, Bauteil2.GND
  N13: Bauteil1.D9, IC2.Enable_2
  N14: Bauteil1.D10, IC2.In_3
  N15: Bauteil1.D11/MOSI, Bauteil2.IN
  N16: Bauteil1.D12/MISO, IC2.In_4
  5V: Bauteil1.5V, Bauteil2.VDD
  N17: IC2.Out_3_(_Controlled_by_Enable_2_), M3.pin_1
  N18: IC2.Out_4_(_Controlled_by_Enable_2_), M3.pin_2

notes:
  Voltage depending on the motors used.

custom parts:
  24 NeoPixel Ring: 24 ultra bright smart LED NeoPixels are arranged in a circle with 2.6" (66mm) outer diameter. The rings are 'chainable' - connect the output pin of one to the input pin of another. Use only one microcontroller pin to control as many as you can chain together! Each LED is addressable as the driver chip is inside the LED. Each one has ~18mA constant current drive so the color will be very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
