# Fritzing sketch Movement_Sketch_v2 (saved by Fritzing 0.9.3b)
circuit board: 7.75755cm x 4.18938cm
breadboards: 1

parts:
  L293D = L293D [package=THT]
  Arduino = Arduino Nano (Rev3.0)
  Motor_2_A = DC Motor
  Motor_1_A = DC Motor
  Battery_12V = Battery block 9V
  Motor_1_B = DC Motor
  Motor_2_B = DC Motor
  Motor_2_C = DC Motor
  Motor_1_C = DC Motor
  C1 = Electrolytic Capacitor [capacitance=100µF package="200 mil [THT, electrolytic]"]
  C2 = Electrolytic Capacitor [capacitance=100µF package="200 mil [THT, electrolytic]"]
  IR_Counter = Max Power IR LED Kit
  IR_Counter1 = Max Power IR LED Kit
  Battery_5V = Battery block 9V

nets:
  N1: L293D.Enable_1, Arduino.D6
  N2: L293D.In_1, Arduino.A4
  N3: L293D.Out_1_(_Controlled_by_Enable_1_), Motor_1_A.pin_2, Motor_1_B.pin_2, Motor_1_C.pin_2
  GND: L293D.0V, Arduino.GND, Battery_12V.-, C1.+, C2.+, IR_Counter.GND, IR_Counter1.GND, Battery_5V.-
  N4: L293D.Out_2_(_Controlled_by_Enable_1_), Motor_1_A.pin_1, Motor_1_B.pin_1, Motor_1_C.pin_1
  N5: L293D.In_2, Arduino.A5
  N6: L293D.+Vmotor, L293D.+V, Battery_12V.+
  N7: L293D.Enable_2, Arduino.D5
  N8: L293D.In_3, Arduino.A3
  N9: L293D.Out_3_(_Controlled_by_Enable_2_), Motor_2_A.pin_1, Motor_2_B.pin_1, Motor_2_C.pin_1
  N10: L293D.Out_4_(_Controlled_by_Enable_2_), Motor_2_A.pin_2, Motor_2_B.pin_2, Motor_2_C.pin_2
  N11: L293D.In_4, Arduino.A2
  N12: Arduino.D2, C1.-, IR_Counter.CONTROL
  N13: Arduino.D3, C2.-, IR_Counter1.CONTROL
  VCC: Arduino.5V, IR_Counter.VCC, IR_Counter1.VCC, Battery_5V.+

notes:
  Voltage depending on the motors used.
