# Fritzing sketch Scanner_Sketch (saved by Fritzing 0.9.3b)
breadboards: 1

parts:
  Bauteil1 = Arduino Nano (Rev3.0)
  hc-sr1 = hc-sr04
  hc-sr2 = hc-sr04

nets:
  GND: Bauteil1.GND, hc-sr1.GND, hc-sr2.GND
  N1: Bauteil1.D7, hc-sr2.Trig
  N2: Bauteil1.D8, hc-sr2.Echo
  N3: Bauteil1.D9, hc-sr1.Trig
  N4: Bauteil1.D10, hc-sr1.Echo
  VCC: Bauteil1.5V, hc-sr1.VCC, hc-sr2.VCC
